// Logisim project FlipFlops.circ as structural Verilog: 2 circuits, main circuit latcher
module latcher (
  input  S,
  input  R,
  output Q,
  output nQ
);

  nor nor_1 (Q, R, nQ);
  nor nor_2 (nQ, Q, S);

  // Notes on the sheet:
  //   LATCHER
  //   Legenda
  //   Q - O output principal.
  //   S - (SET) Quando verdadeiro, seta o estado para 1.
  //   nQ - O oposto do output principal. Presente por convenção.
  //   R
  //   S
  //   0
  //   0
  //   0
  //   1
  //   1
  //   0
  //   1
  //   1
  //   R - (RESET) Quando verdadeiro, ignora o set e reseta o estado para 0.
  //   Tabela de Verdade Reduzida
  //   Q
  //   nQ
  //   0/1
  //   1/0
  //   0
  //   1
  //   1
  //   0
  //   0
  //   0
  //   R
  //   Qa
  //   S
  //   0
  //   0
  //   0
  //   0
  //   0
  //   1
  //   0
  //   1
  //   0
  //   0
  //   1
  //   1
  //   1
  //   0
  //   0
  //   1
  //   0
  //   1
  //   1
  //   1
  //   0
  //   1
  //   1
  //   1
  //   Tabela de Verdade Extendida
  //   Q
  //   nQ
  //   0
  //   1
  //   1
  //   0
  //   0
  //   1
  //   0
  //   1
  //   1
  //   0
  //   1
  //   0
  //   0
  //   1
  //   0
  //   1
  //   Qa - Estado anterior.
endmodule

module main (
  input  in_1,
  input  in_2
);

  wire latcher_1_nq, latcher_1_q;

  LED led_1 (.in(latcher_1_q));
  latcher latcher_1 (.S(in_1), .R(in_2), .Q(latcher_1_q), .nQ(latcher_1_nq));
  LED led_2 (.in(latcher_1_nq));
endmodule
